# Fritzing sketch station (saved by Fritzing 0.9.2b)
circuit board: 8.46667cm x 5.64444cm
breadboards: 1

parts:
  U1 = ESP8266-12 WiFi Module [part_number=ESP8266]
  OLED1 = 128x64 Monochrom OLED Display with SPI Control

nets:
  N1: U1.GPIO_0, OLED1.DC
  N2: U1.CH_PD, OLED1.RST
  GND: U1.GND, OLED1.GND
  N3: U1.GPIO_14, OLED1.D0
  N4: U1.GPIO_13, OLED1.D1
  VCC: U1.VCC, OLED1.VCC

custom parts:
  ESP8266-12 WiFi Module: Generic WiFi Module based on the ESP8266 with onboard PCB antenna and UART communications
